// Logisim project circuit.circ as structural Verilog: 1 circuit, main circuit main
module main (
);

  wire AC_out, ADD_out, bcd_to_7_segment_decoder_2_p1, bcd_to_7_segment_decoder_4_p1,
       binary_to_bcd_converter_1_p2, binary_to_bcd_converter_1_p5, binary_to_bcd_converter_2_p2,
       binary_to_bcd_converter_2_p5, button_1_out, button_2_out, button_3_out, button_4_out, button_5_out,
       button_6_out, button_7_out, button_8_out, C_out, DIV_out, MUL_out, not_1_out, or_1_out,
       priority_encoder_1_gs, SUB_out;
  wire [1:0] priority_encoder_1_out;
  wire [7:0] adder_1_out, divider_1_out, multiplexer_1_out, multiplier_1_out, register_1_q, subtractor_1_out,
       t_ff_8_q;

  Button C (.out(C_out));
  T_Flip_Flop t_ff_1 (.T(1'b1), .clk(button_1_out), .Q(t_ff_8_q[7]), .reset(or_1_out));  // open: Qn, preset
  or or_1 (or_1_out, AC_out, C_out);
  Button button_1 (.out(button_1_out));
  Button button_2 (.out(button_2_out));
  LED led_1 (.in(t_ff_8_q[7]));
  LED led_2 (.in(t_ff_8_q[6]));
  Button AC (.out(AC_out));
  Button ADD (.out(ADD_out));
  LED led_3 (.in(register_1_q[7]));
  LED led_4 (.in(register_1_q[6]));
  T_Flip_Flop t_ff_2 (.T(1'b1), .clk(button_2_out), .Q(t_ff_8_q[6]), .reset(or_1_out));  // open: Qn, preset
  Button button_3 (.out(button_3_out));
  Button button_4 (.out(button_4_out));
  Button button_5 (.out(button_5_out));
  LED led_5 (.in(t_ff_8_q[5]));
  LED led_6 (.in(t_ff_8_q[4]));
  LED led_7 (.in(t_ff_8_q[3]));
  Button SUB (.out(SUB_out));
  Button MUL (.out(MUL_out));
  LED led_8 (.in(register_1_q[5]));
  LED led_9 (.in(register_1_q[4]));
  LED led_10 (.in(register_1_q[3]));
  T_Flip_Flop t_ff_3 (.T(1'b1), .clk(button_3_out), .Q(t_ff_8_q[5]), .reset(or_1_out));  // open: Qn, preset
  Button button_6 (.out(button_6_out));
  Button button_7 (.out(button_7_out));
  Button button_8 (.out(button_8_out));
  LED led_11 (.in(t_ff_8_q[2]));
  LED led_12 (.in(t_ff_8_q[1]));
  LED led_13 (.in(t_ff_8_q[0]));
  Button DIV (.out(DIV_out));
  LED led_14 (.in(register_1_q[2]));
  LED led_15 (.in(register_1_q[1]));
  LED led_16 (.in(register_1_q[0]));
  T_Flip_Flop t_ff_4 (.T(1'b1), .clk(button_4_out), .Q(t_ff_8_q[4]), .reset(or_1_out));  // open: Qn, preset
  Priority_Encoder #(.select(2)) priority_encoder_1 (
    .in0(ADD_out), .in1(SUB_out), .in2(MUL_out), .in3(DIV_out), .out(priority_encoder_1_out),
    .gs(priority_encoder_1_gs));  // open: en_out, en_in
  T_Flip_Flop t_ff_5 (.T(1'b1), .clk(button_5_out), .Q(t_ff_8_q[3]), .reset(or_1_out));  // open: Qn, preset
  Adder adder_1 (.a(register_1_q), .b(t_ff_8_q), .out(adder_1_out));  // open: cin, cout
  Subtractor subtractor_1 (.a(register_1_q), .b(t_ff_8_q), .out(subtractor_1_out));  // open: bin, bout
  Multiplier multiplier_1 (.a(register_1_q), .b(t_ff_8_q), .out(multiplier_1_out));  // open: cin, cout
  Divider divider_1 (.a(register_1_q), .b(t_ff_8_q), .out(divider_1_out));  // open: upper, rem
  T_Flip_Flop t_ff_6 (.T(1'b1), .clk(button_6_out), .Q(t_ff_8_q[2]), .reset(or_1_out));  // open: Qn, preset
  T_Flip_Flop t_ff_7 (.T(1'b1), .clk(button_7_out), .Q(t_ff_8_q[1]), .reset(or_1_out));  // open: Qn, preset
  T_Flip_Flop t_ff_8 (.T(1'b1), .clk(button_8_out), .Q(t_ff_8_q[0]), .reset(or_1_out));  // open: Qn, preset
  Register register_1 (.D(multiplexer_1_out), .clk(not_1_out), .Q(register_1_q), .clr(AC_out));  // open: en
  Multiplexer #(.select(2), .width(8)) multiplexer_1 (
    .in0(adder_1_out), .in1(subtractor_1_out), .in2(multiplier_1_out), .in3(divider_1_out),
    .out(multiplexer_1_out), .sel(priority_encoder_1_out));
  not not_1 (not_1_out, priority_encoder_1_gs);
  _7_Segment_Display u_7_segment_display_1 ();  // open: g, f, a, b, e, d, c, dp
  _7_Segment_Display u_7_segment_display_2 ();  // open: g, f, a, b, e, d, c, dp
  // BCD_to_7_Segment_decoder bcd_to_7_segment_decoder_1: pin names not known
  // BCD_to_7_Segment_decoder bcd_to_7_segment_decoder_2: pin names not known; wires that end beside it: bcd_to_7_segment_decoder_2_p1
  // Binary_to_BCD_converter #(.binvalue(8)) binary_to_bcd_converter_1: pin names not known; wires that end beside it: t_ff_8_q, binary_to_bcd_converter_1_p2, binary_to_bcd_converter_1_p2, bcd_to_7_segment_decoder_2_p1, binary_to_bcd_converter_1_p5
  _7_Segment_Display u_7_segment_display_3 ();  // open: g, f, a, b, e, d, c, dp
  _7_Segment_Display u_7_segment_display_4 ();  // open: g, f, a, b, e, d, c, dp
  // BCD_to_7_Segment_decoder bcd_to_7_segment_decoder_3: pin names not known
  // BCD_to_7_Segment_decoder bcd_to_7_segment_decoder_4: pin names not known; wires that end beside it: bcd_to_7_segment_decoder_4_p1
  // Binary_to_BCD_converter #(.binvalue(8)) binary_to_bcd_converter_2: pin names not known; wires that end beside it: register_1_q, binary_to_bcd_converter_2_p2, binary_to_bcd_converter_2_p2, bcd_to_7_segment_decoder_4_p1, binary_to_bcd_converter_2_p5
  _7_Segment_Display u_7_segment_display_5 ();  // open: g, f, a, b, e, d, c, dp
  // BCD_to_7_Segment_decoder bcd_to_7_segment_decoder_5: pin names not known; wires that end beside it: binary_to_bcd_converter_1_p5
  _7_Segment_Display u_7_segment_display_6 ();  // open: g, f, a, b, e, d, c, dp
  // BCD_to_7_Segment_decoder bcd_to_7_segment_decoder_6: pin names not known; wires that end beside it: binary_to_bcd_converter_2_p5

  // Notes on the sheet:
  //   Input
  //   Operation
  //   Output
endmodule
